# Fritzing sketch SensorXIAO (saved by Fritzing 1.0.3b)

parts:
  U1 = XIAO ESP32C6 [part_number=" XIAO ESP32C6"]
  U2 = LIPO-1000mAh [package=lipo-1000]
  R1 = Resistor [tolerance=±5% power=0.25W resistance=220k package=THT]
  R2 = Resistor [tolerance=±5% power=0.25W resistance=220k package=THT]
  C1_100n = Capacitor [package=cap-pth-small2]

nets:
  N1: U1.D0, R1.Pin_1, R2.Pin_0, C1_100n.1
  N2: U1.GND, R1.Pin_0
  N3: U2.+, R2.Pin_1

custom parts:
  XIAO ESP32C6: XIAO ESP32C6 is a cost-effective MCU based on Espressif’s ESP32-C6. This compact MCU excels in Matter-compliant smart home applications with its support for various wireless connectivity (2.4GHz Wi-Fi 6, BLE 5.0, Zigbee, and Thread). Designed with the thumb-size footprint and a single-sided mount of the XIAO Series, it's perfect for space-limited projects. Encrypted on the chip, the XIAO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
